# Fritzing sketch circuit (saved by Fritzing 0.8.7b)
breadboards: 1

parts:
  GEMMA1 = Adafruit GEMMA
  R1 = Resistor [tolerance=±5% resistance=220 package=THT]
  LED1 = LED - 5mm [color="Red (633nm)" package="5 mm [THT]"]

nets:
  N1: GEMMA1.GND, LED1.cathode
  N2: GEMMA1.D2/A1, R1.Pin_1
  N3: R1.Pin_0, LED1.anode

custom parts:
  Adafruit GEMMA: Adafruit Gemma wearable electronics main board.
